# Fritzing sketch Schematics (saved by Fritzing 0.9.3b)
breadboards: 1

parts:
  Mod1 = Raspberry Pi Pico W
  hc-sr1 = hc-sr04
  S1 = Pushbutton [package="[THT]"]
  LED1 = smd LED [color="Red (633nm)" package="1206 [SMD]"]
  LED2 = smd LED [color="Blue (430nm)" package="1206 [SMD]"]
  R1 = Resistor [tolerance=±5% resistance=220 package="0805 [SMD]"]

nets:
  N1: Mod1.pin_2, R1.Pin_1
  N2: Mod1.pin_3, Mod1.pin_8, Mod1.pin_13, Mod1.pin_18, Mod1.pin_23, Mod1.pin_28, Mod1.pin_33, Mod1.pin_38, Mod1.pin_42, hc-sr1.VCC, S1.Pin_1, S1.Pin_2, LED1.cathode, LED2.cathode
  N3: Mod1.pin_15, hc-sr1.Trig
  N4: Mod1.pin_16, hc-sr1.Echo
  N5: Mod1.pin_21, S1.Pin_3, S1.Pin_4
  N6: Mod1.pin_36, hc-sr1.GND
  N7: LED1.anode, R1.Pin_0

notes:
  ACTIVE SPEAKER

custom parts:
  Raspberry Pi Pico W: Raspberry Pi Pico W. Based around the RP2040 microcontroller the Pico W is a low cost microcontroller device bringing Raspberry Pi quality, cost, and easy of use to the microcontroller space. The areas marked KEEPOUT in pcb silkscreen should not have traces running through them to avoid shorts on a soldered in module!
